# Fritzing sketch Circuit_diagram (saved by Fritzing 0.9.3b)
breadboards: 1

parts:
  Raspberry_Pi_1 = Raspberry Pi 3 [part_number=RPI-3-V1.2]
  R1 = Photocell (LDR) [package=THT]
  R2 = Resistor [tolerance=±5% resistance=10k package=THT]
  LED1 = LED - 3mm [color="Blue (505nm)" package="3 mm [THT]"]
  R3 = Resistor [tolerance=±5% resistance=470 package="1206 [SMD]"]

nets:
  N1: Raspberry_Pi_1.GPIO17, R1.pin_1, R2.Pin_0
  N2: Raspberry_Pi_1.GPIO18, R3.Pin_1
  N3: Raspberry_Pi_1.GND, R2.Pin_1, LED1.cathode
  N4: Raspberry_Pi_1.5V, R1.pin_0
  N5: LED1.anode, R3.Pin_0

notes:
  pin 11 - LDR (in) with 10K resistor
  pin 12 - LED (out) with 470E resistor
