# Fritzing sketch Circuit_diagram (saved by Fritzing 0.9.3b)
breadboards: 1

parts:
  Raspberry_Pi_1 = Raspberry Pi 3 [part_number=RPI-3-V1.2]
  LED1 = LED - 3mm [color="Blue (505nm)" package="3 mm [THT]"]
  R3 = Resistor [tolerance=±5% resistance=1k package="1206 [SMD]"]

nets:
  N1: Raspberry_Pi_1.GPIO22, R3.Pin_1
  N2: Raspberry_Pi_1.GND, LED1.cathode
  N3: LED1.anode, R3.Pin_0

notes:
  pin 15 - LED (out) with 1k resistor
