# Fritzing sketch Circuit_diagram (saved by Fritzing 0.9.3b)
breadboards: 1

parts:
  Raspberry_Pi_2 = Raspberry Pi 3 [part_number=RPI-3-V1.2]
  EDGY_motor_control1 = EDGY
  VCC1 = Battery block 9V
  R1 = Resistor [tolerance=±5% resistance=10k package=THT]
  R2 = Resistor [tolerance=±5% resistance=10k package=THT]
  R3 = Resistor [tolerance=±5% resistance=2.20k package=THT]
  S1 = Pushbutton [package="[THT]"]
  C1 = Electrolytic Capacitor [capacitance=1μF voltage=5.0V package="0405 [SMD, electrolytic]"]
  M1 = DC Motor

nets:
  N1: Raspberry_Pi_2.GIPO17, R3.Pin_1, C1.+
  GND: Raspberry_Pi_2.GND, EDGY_motor_control1.GND, VCC1.-, S1.Pin_1, S1.Pin_2, C1.-
  N2: Raspberry_Pi_2.GIPO18, EDGY_motor_control1.A2
  N3: Raspberry_Pi_2.5V, EDGY_motor_control1.5V+, R1.Pin_1
  N4: EDGY_motor_control1.B2out, M1.pin_2
  N5: EDGY_motor_control1.A2out, M1.pin_1
  N6: R1.Pin_0, R2.Pin_0, S1.Pin_3, S1.Pin_4
  N7: R2.Pin_1, R3.Pin_0

notes:
  R1 - 10K (Pull Up Resistor)
  R2+R3 - 10K+2.2K = 12.2 K Resistor
  R2+R3 - C1 = RC Debounce Circuit
  Motor Board actually used is different from the ciruit motor control.
