# Fritzing sketch Circuit_diagram (saved by Fritzing 0.9.3b)
breadboards: 1

parts:
  Raspberry_Pi_1 = Raspberry Pi 3 [part_number=RPI-3-V1.2]
  R1 = Resistor [tolerance=±5% resistance=2.2k package=THT]
  R2 = Resistor [tolerance=±5% resistance=1k package="1206 [SMD]"]
  hc-sr1 = hc-sr04

nets:
  N1: Raspberry_Pi_1.GPIO17, hc-sr1.Trig
  N2: Raspberry_Pi_1.GPIO18, R1.Pin_1, R2.Pin_0
  GND: Raspberry_Pi_1.GND, R2.Pin_1, hc-sr1.GND
  5V: Raspberry_Pi_1.5V, hc-sr1.VCC
  N3: R1.Pin_0, hc-sr1.Echo

notes:
  pin 11 - TRIGGER (out)
  pin 12 - ECHO (in)
  R1 - 2.2K
  R2 - 1K
